# Fritzing sketch wssf_client (saved by Fritzing 0.9.4)
breadboards: 1

parts:
  Nano1 = Arduino Nano v2.3
  Part1 = NRF24L01+ Breakout Board
  LED1 = LED - 5mm [color="Red (633nm)" package="5 mm [THT]"]
  R1 = Resistor [tolerance=±5% resistance=220 package=THT]
  R2 = Resistor [tolerance=±5% resistance=220 package=THT]
  R3 = Resistor [tolerance=±5% resistance=220 package=THT]
  R4 = Resistor [tolerance=±5% resistance=10k package=THT]
  S1 = Pushbutton [package="[THT]"]

nets:
  GND: Nano1.GND, Part1.GND, R1.Pin_1, R4.Pin_1
  N1: Nano1.D2, R2.Pin_1
  N2: Nano1.D3, R4.Pin_0, S1.Pin_3, S1.Pin_4
  N3: Nano1.D4, R3.Pin_1
  N4: Nano1.D5, LED1.cathode
  3V3: Nano1.3V3, Part1.VCC, S1.Pin_1, S1.Pin_2
  N5: LED1.anode, R1.Pin_0
  N6: R2.Pin_0, R3.Pin_0
