# Fritzing sketch wssf_server (saved by Fritzing 0.9.4)
breadboards: 1

parts:
  Nano2 = Arduino Nano v2.3
  Part2 = NRF24L01+ Breakout Board
  Part3 = 12 NeoPixel Ring [part_number=1643]
  C1 = Electrolytic Capacitor [capacitance=10µF package="100 mil [THT, electrolytic]"]

nets:
  GND: Nano2.GND, Part2.GND, Part3.GND, C1.-
  N1: Nano2.D3, Part3.IN
  N2: Nano2.D7, Part2.CE
  N3: Nano2.D8, Part2.CS
  N4: Nano2.D11, Part2.MOSI
  N5: Nano2.D12, Part2.MISO
  N6: Nano2.D13, Part2.SCK
  3V3: Nano2.3V3, Part2.VCC, Part3.VDD, C1.+

custom parts:
  12 NeoPixel Ring: 12 ultra bright smart LED NeoPixels are arranged in a circle with 1.5" (37mm) outer diameter. The rings are 'chainable' - connect the output pin of one to the input pin of another. Use only one microcontroller pin to control as many as you can chain together! Each LED is addressable as the driver chip is inside the LED. Each one has ~18mA constant current drive so the color will be very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
